// Logisim project adder_4.circ as structural Verilog: 1 circuit, main circuit main
module main (
  input  M,
  input  a0,
  input  b0,
  input  a1,
  input  b1,
  input  a2,
  input  b2,
  input  a3,
  input  b3,
  output s0,
  output s1,
  output s2,
  output s3,
  output CO
);

  wire adder_1_cout, adder_2_cout, adder_3_cout, undriven, xor_1_out, xor_2_out, xor_3_out, xor_4_out;

  xor xor_1 (xor_1_out, M, b0);
  xor xor_2 (xor_2_out, M, b1);
  xor xor_3 (xor_3_out, M, b2);
  xor xor_4 (xor_4_out, M, b3);
  Adder #(.width(1)) adder_1 (.a(a0), .b(xor_1_out), .out(s0), .cin(undriven), .cout(adder_1_cout));
  Adder #(.width(1)) adder_2 (.a(a1), .b(xor_2_out), .out(s1), .cin(adder_1_cout), .cout(adder_2_cout));
  Adder #(.width(1)) adder_3 (.a(a2), .b(xor_3_out), .out(s2), .cin(adder_2_cout), .cout(adder_3_cout));
  Adder #(.width(1)) adder_4 (.a(a3), .b(xor_4_out), .out(s3), .cin(adder_3_cout), .cout(CO));

  // Notes on the sheet:
  //   ??
endmodule
