// Logisim project Prep - Shift Register.circ as structural Verilog: 1 circuit, main circuit main
module main (
  input  Input,
  output out_2
);

  wire button_1_out, button_2_out, d_ff_1_q, d_ff_2_q, d_ff_3_q;

  Button button_1 (.out(button_1_out));
  Button button_2 (.out(button_2_out));
  D_Flip_Flop #(.trigger("rising")) d_ff_1 (
    .clk(button_1_out), .D(Input), .Q(d_ff_1_q), .reset(button_2_out));  // open: Qn, preset, en
  D_Flip_Flop #(.trigger("rising")) d_ff_2 (
    .clk(button_1_out), .D(d_ff_1_q), .Q(d_ff_2_q), .reset(button_2_out));  // open: Qn, preset, en
  D_Flip_Flop #(.trigger("rising")) d_ff_3 (
    .clk(button_1_out), .D(d_ff_2_q), .Q(d_ff_3_q), .reset(button_2_out));  // open: Qn, preset, en
  D_Flip_Flop #(.trigger("rising")) d_ff_4 (
    .clk(button_1_out), .D(d_ff_3_q), .Q(out_2), .reset(button_2_out));  // open: Qn, preset, en

  // Notes on the sheet:
  //   Clock
  //   Reset
endmodule
