// Logisim project Prep - Sync Counter.circ as structural Verilog: 1 circuit, main circuit Sync Counter
module Sync_Counter (
);

  wire button_1_out, button_2_out, d_ff_1_q, d_ff_1_qn, d_ff_2_q, d_ff_2_qn, d_ff_3_q, d_ff_3_qn, nand_1_out,
       nand_2_out, nand_3_out, nand_4_out, xor_1_out;

  Button button_1 (.out(button_1_out));
  Button button_2 (.out(button_2_out));
  D_Flip_Flop #(.trigger("rising")) d_ff_1 (
    .clk(button_1_out), .D(d_ff_1_qn), .Q(d_ff_1_q), .Qn(d_ff_1_qn), .reset(button_2_out));  // open: preset, en
  xor xor_1 (xor_1_out, d_ff_2_q, d_ff_1_q);
  nand nand_1 (nand_1_out, d_ff_3_q, d_ff_1_qn);
  nand nand_2 (nand_2_out, d_ff_3_qn, d_ff_2_q, d_ff_1_q);
  D_Flip_Flop #(.trigger("rising")) d_ff_2 (
    .clk(button_1_out), .D(xor_1_out), .Q(d_ff_2_q), .Qn(d_ff_2_qn), .reset(button_2_out));  // open: preset, en
  D_Flip_Flop #(.trigger("rising")) d_ff_3 (
    .clk(button_1_out), .D(nand_4_out), .Q(d_ff_3_q), .Qn(d_ff_3_qn), .reset(button_2_out));  // open: preset, en
  nand nand_3 (nand_3_out, d_ff_3_q, d_ff_2_qn);
  nand nand_4 (nand_4_out, nand_3_out, nand_1_out, nand_2_out);

  // Notes on the sheet:
  //   Clock
  //   Reset
endmodule
