// Logisim project Challenge.circ as structural Verilog: 1 circuit, main circuit Programmable Combination Lock XORs
module Programmable_Combination_Lock_XORs (
  input  MSB,
  input  in_2,
  input  in_3,
  input  LSB,
  input  MSB_2,
  input  in_6,
  input  in_7,
  input  LSB_2
);

  wire and_1_out, and_2_out, and_3_out, and_4_out, and_5_out, and_6_out, and_7_out, and_8_out, and_9_out,
       and_10_out, and_11_out, and_12_out, and_13_out, and_14_out, button_1_out, button_2_out, button_3_out,
       button_4_out, d_ff_1_qn, d_ff_2_qn, d_ff_6_qn, d_ff_9_qn, nand_1_out, nand_2_out, nand_3_out,
       nand_4_out, nand_5_out, nand_6_out, nand_7_out, nand_8_out, nand_9_out, nand_10_out, xor_1_out,
       xor_2_out, xor_3_out, xor_4_out, xor_5_out, xor_6_out, xor_7_out, xor_8_out;
  wire [3:0] d_ff_13_q, d_ff_14_q, d_ff_15_q, d_ff_16_q;

  Button button_1 (.out(button_1_out));
  Button button_2 (.out(button_2_out));
  Button button_3 (.out(button_3_out));
  Button button_4 (.out(button_4_out));
  D_Flip_Flop #(.trigger("rising")) d_ff_1 (
    .clk(button_1_out), .D(MSB), .Q(d_ff_13_q[3]), .Qn(d_ff_1_qn), .reset(button_2_out));  // open: preset, en
  D_Flip_Flop #(.trigger("rising")) d_ff_2 (
    .clk(button_1_out), .D(d_ff_13_q[3]), .Q(d_ff_14_q[3]), .Qn(d_ff_2_qn), .reset(button_2_out));  // open: preset, en
  D_Flip_Flop #(.trigger("rising")) d_ff_3 (
    .clk(button_3_out), .D(d_ff_16_q[3]), .Q(d_ff_15_q[3]), .reset(button_4_out));  // open: Qn, preset, en
  D_Flip_Flop #(.trigger("rising")) d_ff_4 (
    .clk(button_3_out), .D(MSB_2), .Q(d_ff_16_q[3]), .reset(button_4_out));  // open: Qn, preset, en
  D_Flip_Flop #(.trigger("rising")) d_ff_5 (
    .clk(button_1_out), .D(in_2), .Q(d_ff_13_q[2]), .reset(button_2_out));  // open: Qn, preset, en
  D_Flip_Flop #(.trigger("rising")) d_ff_6 (
    .clk(button_1_out), .D(d_ff_13_q[2]), .Q(d_ff_14_q[2]), .Qn(d_ff_6_qn), .reset(button_2_out));  // open: preset, en
  D_Flip_Flop #(.trigger("rising")) d_ff_7 (
    .clk(button_3_out), .D(d_ff_16_q[2]), .Q(d_ff_15_q[2]), .reset(button_4_out));  // open: Qn, preset, en
  D_Flip_Flop #(.trigger("rising")) d_ff_8 (
    .clk(button_3_out), .D(in_6), .Q(d_ff_16_q[2]), .reset(button_4_out));  // open: Qn, preset, en
  D_Flip_Flop #(.trigger("rising")) d_ff_9 (
    .clk(button_1_out), .D(in_3), .Q(d_ff_13_q[1]), .Qn(d_ff_9_qn), .reset(button_2_out));  // open: preset, en
  D_Flip_Flop #(.trigger("rising")) d_ff_10 (
    .clk(button_1_out), .D(d_ff_13_q[1]), .Q(d_ff_14_q[1]), .reset(button_2_out));  // open: Qn, preset, en
  D_Flip_Flop #(.trigger("rising")) d_ff_11 (
    .clk(button_3_out), .D(d_ff_16_q[1]), .Q(d_ff_15_q[1]), .reset(button_4_out));  // open: Qn, preset, en
  D_Flip_Flop #(.trigger("rising")) d_ff_12 (
    .clk(button_3_out), .D(in_7), .Q(d_ff_16_q[1]), .reset(button_4_out));  // open: Qn, preset, en
  D_Flip_Flop #(.trigger("rising")) d_ff_13 (
    .clk(button_1_out), .D(LSB), .Q(d_ff_13_q[0]), .reset(button_2_out));  // open: Qn, preset, en
  D_Flip_Flop #(.trigger("rising")) d_ff_14 (
    .clk(button_1_out), .D(d_ff_13_q[0]), .Q(d_ff_14_q[0]), .reset(button_2_out));  // open: Qn, preset, en
  D_Flip_Flop #(.trigger("rising")) d_ff_15 (
    .clk(button_3_out), .D(d_ff_16_q[0]), .Q(d_ff_15_q[0]), .reset(button_4_out));  // open: Qn, preset, en
  D_Flip_Flop #(.trigger("rising")) d_ff_16 (
    .clk(button_3_out), .D(LSB_2), .Q(d_ff_16_q[0]), .reset(button_4_out));  // open: Qn, preset, en
  and and_1 (and_1_out, d_ff_1_qn, d_ff_13_q[2]);
  and and_2 (and_2_out, d_ff_9_qn, d_ff_13_q[0]);
  xor xor_1 (xor_1_out, d_ff_13_q[0], d_ff_16_q[0]);
  xor xor_2 (xor_2_out, d_ff_13_q[1], d_ff_16_q[1]);
  xor xor_3 (xor_3_out, d_ff_13_q[2], d_ff_16_q[2]);
  xor xor_4 (xor_4_out, d_ff_13_q[3], d_ff_16_q[3]);
  and and_3 (and_3_out, and_1_out, and_2_out);
  Hex_Digit_Display hex_digit_display_1 (.value(d_ff_13_q));  // open: dp
  and and_4 (and_4_out, and_3_out, and_7_out);
  and and_5 (and_5_out, d_ff_14_q[0], d_ff_14_q[1]);
  and and_6 (and_6_out, d_ff_6_qn, d_ff_2_qn);
  Hex_Digit_Display hex_digit_display_2 (.value(d_ff_14_q));  // open: dp
  nand nand_1 (nand_1_out, and_4_out, and_4_out);
  and and_7 (and_7_out, and_5_out, and_6_out);
  nand nand_2 (nand_2_out, xor_1_out, xor_1_out);
  nand nand_3 (nand_3_out, xor_2_out, xor_2_out);
  nand nand_4 (nand_4_out, xor_3_out, xor_3_out);
  nand nand_5 (nand_5_out, xor_4_out, xor_4_out);
  LED led_1 (.in(and_4_out));
  LED led_2 (.in(nand_1_out));
  Hex_Digit_Display hex_digit_display_3 (.value(d_ff_16_q));  // open: dp
  and and_8 (and_8_out, nand_2_out, nand_3_out);
  and and_9 (and_9_out, nand_4_out, nand_5_out);
  Hex_Digit_Display hex_digit_display_4 (.value(d_ff_15_q));  // open: dp
  xor xor_5 (xor_5_out, d_ff_14_q[3], d_ff_15_q[3]);
  xor xor_6 (xor_6_out, d_ff_14_q[2], d_ff_15_q[2]);
  xor xor_7 (xor_7_out, d_ff_14_q[1], d_ff_15_q[1]);
  xor xor_8 (xor_8_out, d_ff_14_q[0], d_ff_15_q[0]);
  and and_10 (and_10_out, and_8_out, and_9_out);
  nand nand_6 (nand_6_out, xor_5_out, xor_5_out);
  nand nand_7 (nand_7_out, xor_6_out, xor_6_out);
  nand nand_8 (nand_8_out, xor_7_out, xor_7_out);
  nand nand_9 (nand_9_out, xor_8_out, xor_8_out);
  and and_11 (and_11_out, and_13_out, and_10_out);
  and and_12 (and_12_out, nand_6_out, nand_7_out);
  and and_13 (and_13_out, and_12_out, and_14_out);
  and and_14 (and_14_out, nand_8_out, nand_9_out);
  LED led_3 (.in(and_11_out));
  nand nand_10 (nand_10_out, and_11_out, and_11_out);
  LED led_4 (.in(nand_10_out));

  // Notes on the sheet:
  //   Enter
  //   Reset
  //   Enter
  //   Reset
  //   Justin Mancinelli
  //   42094353
  //   Correct Combination: 53
  //   Input Combo
  //   This box should be
  //   removed from final
  //   design as it is obsolete
  //   with the programmable
  //   interface
  //   Programmed Combo
  //   Open
  //   Close
  //   Open
  //   Close
  //   Open
  //   Close
endmodule
