// Logisim project Challenge2.circ as structural Verilog: 1 circuit, main circuit Programmable Combination Lock MUXs
module Programmable_Combination_Lock_MUXs (
  input  MSB,
  input  Programmer,
  input  in_3,
  input  LSB,
  input  MSB_2,
  input  in_6,
  input  in_7,
  input  LSB_2,
  input  LSB_3,
  input  Programmer_2,
  input  Units,
  input  MSB_3
);

  wire and_1_out, and_2_out, and_3_out, and_4_out, and_5_out, and_6_out, and_7_out, button_1_out,
       button_2_out, d_ff_1_qn, d_ff_2_qn, d_ff_3_qn, d_ff_4_qn, d_ff_5_qn, d_ff_6_qn, d_ff_7_qn, d_ff_8_qn,
       multiplexer_1_out, multiplexer_2_out, multiplexer_3_out, multiplexer_4_out, multiplexer_5_out,
       multiplexer_6_out, multiplexer_7_out, multiplexer_8_out, nand_1_out;
  wire [3:0] d_ff_7_q, d_ff_8_q;

  Button button_1 (.out(button_1_out));
  Button button_2 (.out(button_2_out));
  Multiplexer #(.select(1), .width(1)) multiplexer_1 (
    .in0(d_ff_7_q[3]), .in1(d_ff_1_qn), .out(multiplexer_1_out), .sel(LSB));
  D_Flip_Flop #(.trigger("rising")) d_ff_1 (
    .clk(button_1_out), .D(MSB_2), .Q(d_ff_7_q[3]), .Qn(d_ff_1_qn), .reset(button_2_out));  // open: preset, en
  D_Flip_Flop #(.trigger("rising")) d_ff_2 (
    .clk(button_1_out), .D(d_ff_7_q[3]), .Q(d_ff_8_q[3]), .Qn(d_ff_2_qn), .reset(button_2_out));  // open: preset, en
  Multiplexer #(.select(1), .width(1)) multiplexer_2 (
    .in0(d_ff_8_q[3]), .in1(d_ff_2_qn), .out(multiplexer_2_out), .sel(LSB_3));
  Multiplexer #(.select(1), .width(1)) multiplexer_3 (
    .in0(d_ff_7_q[2]), .in1(d_ff_3_qn), .out(multiplexer_3_out), .sel(in_3));
  D_Flip_Flop #(.trigger("rising")) d_ff_3 (
    .clk(button_1_out), .D(in_6), .Q(d_ff_7_q[2]), .Qn(d_ff_3_qn), .reset(button_2_out));  // open: preset, en
  D_Flip_Flop #(.trigger("rising")) d_ff_4 (
    .clk(button_1_out), .D(d_ff_7_q[2]), .Q(d_ff_8_q[2]), .Qn(d_ff_4_qn), .reset(button_2_out));  // open: preset, en
  D_Flip_Flop #(.trigger("rising")) d_ff_5 (
    .clk(button_1_out), .D(in_7), .Q(d_ff_7_q[1]), .Qn(d_ff_5_qn), .reset(button_2_out));  // open: preset, en
  D_Flip_Flop #(.trigger("rising")) d_ff_6 (
    .clk(button_1_out), .D(d_ff_7_q[1]), .Q(d_ff_8_q[1]), .Qn(d_ff_6_qn), .reset(button_2_out));  // open: preset, en
  Multiplexer #(.select(1), .width(1)) multiplexer_4 (
    .in0(d_ff_8_q[2]), .in1(d_ff_4_qn), .out(multiplexer_4_out), .sel(Programmer_2));
  Multiplexer #(.select(1), .width(1)) multiplexer_5 (
    .in0(d_ff_7_q[1]), .in1(d_ff_5_qn), .out(multiplexer_5_out), .sel(Programmer));
  D_Flip_Flop #(.trigger("rising")) d_ff_7 (
    .clk(button_1_out), .D(LSB_2), .Q(d_ff_7_q[0]), .Qn(d_ff_7_qn), .reset(button_2_out));  // open: preset, en
  D_Flip_Flop #(.trigger("rising")) d_ff_8 (
    .clk(button_1_out), .D(d_ff_7_q[0]), .Q(d_ff_8_q[0]), .Qn(d_ff_8_qn), .reset(button_2_out));  // open: preset, en
  Multiplexer #(.select(1), .width(1)) multiplexer_6 (
    .in0(d_ff_8_q[1]), .in1(d_ff_6_qn), .out(multiplexer_6_out), .sel(Units));
  Multiplexer #(.select(1), .width(1)) multiplexer_7 (
    .in0(d_ff_7_q[0]), .in1(d_ff_7_qn), .out(multiplexer_7_out), .sel(MSB));
  and and_1 (and_1_out, multiplexer_1_out, multiplexer_3_out);
  and and_2 (and_2_out, multiplexer_5_out, multiplexer_7_out);
  Multiplexer #(.select(1), .width(1)) multiplexer_8 (
    .in0(d_ff_8_q[0]), .in1(d_ff_8_qn), .out(multiplexer_8_out), .sel(MSB_3));
  and and_3 (and_3_out, and_1_out, and_2_out);
  Hex_Digit_Display hex_digit_display_1 (.value(d_ff_7_q));  // open: dp
  and and_4 (and_4_out, and_3_out, and_7_out);
  and and_5 (and_5_out, multiplexer_8_out, multiplexer_6_out);
  and and_6 (and_6_out, multiplexer_4_out, multiplexer_2_out);
  Hex_Digit_Display hex_digit_display_2 (.value(d_ff_8_q));  // open: dp
  nand nand_1 (nand_1_out, and_4_out, and_4_out);
  and and_7 (and_7_out, and_5_out, and_6_out);
  LED led_1 (.in(and_4_out));
  LED led_2 (.in(nand_1_out));
  Hex_Digit_Display hex_digit_display_3 (.value({MSB, Programmer, in_3, LSB}));  // open: dp
  Hex_Digit_Display hex_digit_display_4 (.value({MSB_3, Units, Programmer_2, LSB_3}));  // open: dp

  // Notes on the sheet:
  //   Programmer
  //   Programmer
  //   Programmer
  //   Tens
  //   User
  //   Enter
  //   Reset
  //   Units
  //   Units
  //   Units
  //   Justin Mancinelli
  //   42094353
  //   Correct Combination: 53
  //   Input Combo
  //   Programmed Combo
  //   Open
  //   Close
  //   Open
  //   Close
endmodule
