// Logisim project Design.circ as structural Verilog: 1 circuit, main circuit Fixed Combination Lock
module Fixed_Combination_Lock (
  input  MSB,
  input  in_2,
  input  in_3,
  input  LSB
);

  wire and_1_out, and_2_out, and_3_out, and_4_out, and_5_out, and_6_out, button_1_out, button_2_out,
       d_ff_1_qn, d_ff_2_qn, d_ff_4_qn, d_ff_5_qn, nand_1_out, nand_2_out;
  wire [3:0] d_ff_7_q, d_ff_8_q;

  Button button_1 (.out(button_1_out));
  Button button_2 (.out(button_2_out));
  D_Flip_Flop #(.trigger("rising")) d_ff_1 (
    .clk(button_1_out), .D(MSB), .Q(d_ff_7_q[3]), .Qn(d_ff_1_qn), .reset(button_2_out));  // open: preset, en
  D_Flip_Flop #(.trigger("rising")) d_ff_2 (
    .clk(button_1_out), .D(d_ff_7_q[3]), .Q(d_ff_8_q[3]), .Qn(d_ff_2_qn), .reset(button_2_out));  // open: preset, en
  D_Flip_Flop #(.trigger("rising")) d_ff_3 (
    .clk(button_1_out), .D(in_2), .Q(d_ff_7_q[2]), .reset(button_2_out));  // open: Qn, preset, en
  D_Flip_Flop #(.trigger("rising")) d_ff_4 (
    .clk(button_1_out), .D(d_ff_7_q[2]), .Q(d_ff_8_q[2]), .Qn(d_ff_4_qn), .reset(button_2_out));  // open: preset, en
  D_Flip_Flop #(.trigger("rising")) d_ff_5 (
    .clk(button_1_out), .D(in_3), .Q(d_ff_7_q[1]), .Qn(d_ff_5_qn), .reset(button_2_out));  // open: preset, en
  D_Flip_Flop #(.trigger("rising")) d_ff_6 (
    .clk(button_1_out), .D(d_ff_7_q[1]), .Q(d_ff_8_q[1]), .reset(button_2_out));  // open: Qn, preset, en
  D_Flip_Flop #(.trigger("rising")) d_ff_7 (
    .clk(button_1_out), .D(LSB), .Q(d_ff_7_q[0]), .reset(button_2_out));  // open: Qn, preset, en
  D_Flip_Flop #(.trigger("rising")) d_ff_8 (
    .clk(button_1_out), .D(d_ff_7_q[0]), .Q(d_ff_8_q[0]), .reset(button_2_out));  // open: Qn, preset, en
  and and_1 (and_1_out, d_ff_1_qn, d_ff_7_q[2]);
  and and_2 (and_2_out, d_ff_5_qn, d_ff_7_q[0]);
  and and_3 (and_3_out, d_ff_8_q[0], d_ff_8_q[1]);
  and and_4 (and_4_out, d_ff_4_qn, d_ff_2_qn);
  and and_5 (and_5_out, and_1_out, and_2_out);
  Hex_Digit_Display hex_digit_display_1 (.value(d_ff_7_q));  // open: dp
  nand nand_1 (nand_1_out, and_5_out, and_6_out);
  and and_6 (and_6_out, and_3_out, and_4_out);
  Hex_Digit_Display hex_digit_display_2 (.value(d_ff_8_q));  // open: dp
  LED led_1 (.in(nand_1_out));
  LED led_2 (.in(nand_2_out));
  nand nand_2 (nand_2_out, nand_1_out, nand_1_out);

  // Notes on the sheet:
  //   Enter
  //   Reset
  //   Justin Mancinelli
  //   42094353
  //   Correct Combination: 53
  //   Close
  //   Open
endmodule
